# Fritzing sketch Tesis (saved by Fritzing 0.9.3b)
circuit board: 8.46667cm x 5.64444cm

parts:
  Componente1 = Arduino Mega 2560 (Rev3)
  Flex1 = Basic Flex Resistor
  5V = DC Power [voltage=5]
  Flex2 = Basic Flex Resistor
  Flex3 = Basic Flex Resistor
  Flex4 = Basic Flex Resistor
  Flex5 = Basic Flex Resistor
  J1 = shrouded pin header, 16 pins [form="♂ (shrouded male)"]
  J2 = shrouded pin header, 16 pins [form="♂ (shrouded male)"]
  R1 = Resistor [tolerance=±5% resistance=47k package=THT]
  R2 = Resistor [tolerance=±5% resistance=47k package=THT]
  R3 = Resistor [tolerance=±5% resistance=47k package=THT]
  R4 = Resistor [tolerance=±5% resistance=47k package=THT]
  R5 = Resistor [tolerance=±5% resistance=47k package=THT]
  MPU6050 = female pin header, 8 pins [form="♀ (female)"]
  GY1 = MPU-6050 Board GY-521 [form="♀ (female)" package=THT]

nets:
  N1: Componente1.A0, J2.pin14
  N2: Componente1.A1, J2.pin6
  N3: Componente1.A2, J2.pin4
  N4: Componente1.A3, J2.pin3
  N5: Componente1.A4, J2.pin11
  N6: Componente1.D21/SCL, J2.pin15
  N7: Componente1.D20/SDA, Componente1.SDA, J2.pin7
  N8: Componente1.GND, 5V.V-
  N9: Componente1.3V3, J2.pin2
  N10: Componente1.5V, 5V.V+, J2.pin1, J2.pin8, J2.pin9, J2.pin16
  N11: Componente1.D2_PWM, J2.pin10
  N12: Flex1.Pin_2, J1.pin14, R1.Pin_1
  N13: Flex1.pin_1, Flex2.pin_1, Flex3.pin_1, Flex4.pin_1, Flex5.pin_1, J1.pin5, J1.pin13, MPU6050.pin2, GY1.pin2
  N14: Flex2.Pin_2, J1.pin6, R2.Pin_1
  N15: Flex3.Pin_2, J1.pin4, R3.Pin_1
  N16: Flex4.Pin_2, J1.pin3, R4.Pin_1
  N17: Flex5.Pin_2, J1.pin11, R5.Pin_1
  N18: J1.pin1, J1.pin16, R1.Pin_0, R2.Pin_0, R3.Pin_0, R4.Pin_0, R5.Pin_0
  N19: J1.pin2, MPU6050.pin1, GY1.pin1
  N20: J1.pin7, MPU6050.pin4, GY1.pin4
  N21: J1.pin10, MPU6050.pin8, GY1.pin8
  N22: J1.pin15, MPU6050.pin3, GY1.pin3
  N23: J2.pin5, J2.pin13

custom parts:
  MPU-6050 Board GY-521: Acelerometro y Giroscopio MPU-6050 Board GY-521
